# Fritzing sketch arduino-basic (saved by Fritzing 0.9.3b)
breadboards: 1

parts:
  元件1 = Arduino Uno (Rev3)
  LED1 = smd LED [color="Red (633nm)" package="0805 [SMD]"]
  S1 = Momentary Switch [package=ksa_sealed_tac_switch]
  R1 = Resistor [tolerance=±5% resistance=220 package=THT]
  R2 = Resistor [tolerance=±5% resistance=220 package=THT]

nets:
  N1: 元件1.D8, S1.4
  N2: 元件1.D9_PWM, R2.Pin_0
  N3: 元件1.5V, S1.1
  N4: 元件1.GND, LED1.cathode, R1.Pin_0
  N5: LED1.anode, R2.Pin_1
  N6: S1.3, R1.Pin_1

// code stored in the sketch: basic.ino
/* Learn to use pushbutton (button switch) with Arduino - Tutorial
   More info and circuit schematic: http://www.ardumotive.com/arduino-tutorials/category/button
   Dev: Michalis Vasilakis / Date: 19/10/2014  
   UPDATED 2/6/2016 - LED to Arduino pin 3 and button to Arduino pin 4*/


//Constants
const int buttonPin = 4;     
const int ledPin =  3;     

//Variables
int buttonState = 0;
int flag=0;

void setup() {
  //Input or output?
  pinMode(ledPin, OUTPUT);      
  pinMode(buttonPin, INPUT_PULLUP);   
}

void loop(){
  //Read button state (pressed or not pressed?)
  buttonState = digitalRead(buttonPin);

  //If button pressed...
  if (buttonState == LOW) { 
    //...ones, turn led on!
    if ( flag == 0){
      digitalWrite(ledPin, HIGH);
      flag=1; //change flag variable
    }
    //...twice, turn led off!
    else if ( flag == 1){
      digitalWrite(ledPin, LOW);
      flag=0; //change flag variable again 
    }    
  }
  delay(200); //Small delay

}
